// Logisim project display7seg.circ as structural Verilog: 1 circuit, main circuit seteSegmentos
module seteSegmentos (
  input  x,
  input  y
);

  wire and_1_out, and_2_out, not_1_out, not_2_out, or_1_out, or_2_out, or_3_out, or_4_out, or_5_out;

  not not_1 (not_1_out, x);
  not not_2 (not_2_out, y);
  or or_1 (or_1_out, not_2_out, x);
  or or_2 (or_2_out, not_2_out, x);
  and and_1 (and_1_out, not_1_out, not_2_out);
  and and_2 (and_2_out, x, y);
  or or_3 (or_3_out, not_2_out, x);
  or or_4 (or_4_out, not_1_out, not_2_out);
  or or_5 (or_5_out, and_1_out, and_2_out);
  _7_Segment_Display u_7_segment_display_1 (
    .g(x), .f(not_1_out), .a(or_1_out), .b(or_2_out), .e(or_4_out), .d(or_3_out), .c(or_5_out));  // open: dp
endmodule
