// Logisim project somadorUso.circ as structural Verilog: 2 circuits, main circuit somador4bits
module somador4bits (
  input  a3,
  input  a2,
  input  a1,
  input  a0,
  input  b3,
  input  b2,
  input  b1,
  input  b0,
  input  C0,
  output out_10,
  output out_11,
  output out_12,
  output out_13,
  output out_14
);

  wire somador_1_cout, somador_2_cout, somador_3_cout;

  somador somador_1 (.b(b0), .Cin(C0), .a(a0), .SUM(out_13), .Cout(somador_1_cout));
  somador somador_2 (.b(b1), .Cin(somador_1_cout), .a(a1), .SUM(out_12), .Cout(somador_2_cout));
  somador somador_3 (.b(b2), .Cin(somador_2_cout), .a(a2), .SUM(out_11), .Cout(somador_3_cout));
  somador somador_4 (.b(b3), .Cin(somador_3_cout), .a(a3), .SUM(out_10), .Cout(out_14));
endmodule

module somador8bits (
  input  C0,
  output [7:0] res,
  output ovflw
);

  wire somador_1_cout, somador_2_cout, somador_3_cout, somador_4_cout, somador_5_cout, somador_6_cout,
       somador_7_cout;
  wire [7:0] a_out, b_out;

  Slider a (.out(a_out));
  Slider b (.out(b_out));
  somador somador_1 (.b(b_out[0]), .Cin(C0), .a(a_out[0]), .SUM(res[0]), .Cout(somador_1_cout));
  somador somador_2 (.b(b_out[1]), .Cin(somador_1_cout), .a(a_out[1]), .SUM(res[1]), .Cout(somador_2_cout));
  somador somador_3 (.b(b_out[2]), .Cin(somador_2_cout), .a(a_out[2]), .SUM(res[2]), .Cout(somador_3_cout));
  somador somador_4 (.b(b_out[3]), .Cin(somador_3_cout), .a(a_out[3]), .SUM(res[3]), .Cout(somador_4_cout));
  somador somador_5 (.b(b_out[4]), .Cin(somador_4_cout), .a(a_out[4]), .SUM(res[4]), .Cout(somador_5_cout));
  somador somador_6 (.b(b_out[5]), .Cin(somador_5_cout), .a(a_out[5]), .SUM(res[5]), .Cout(somador_6_cout));
  somador somador_7 (.b(b_out[6]), .Cin(somador_6_cout), .a(a_out[6]), .SUM(res[6]), .Cout(somador_7_cout));
  somador somador_8 (.b(b_out[7]), .Cin(somador_7_cout), .a(a_out[7]), .SUM(res[7]), .Cout(ovflw));
endmodule
